# Fritzing sketch neoPixelCircularDisplayTest (saved by Fritzing 0.7.9b)
breadboards: 1

parts:
  LED1 = Adafruit_FLORA_RGB_Smart_Pixel
  Arduino1 = Arduino

nets:
  N1: LED1.connector1, Arduino1.+5V
  N2: LED1.connector2, Arduino1.D2
  N3: LED1.connector3, Arduino1.GND
