# Fritzing sketch sequentialStatusSwitcher (saved by Fritzing 0.8.3b)
breadboards: 1

parts:
  Componente1 = Arduino Uno (Rev3)
  S1 = Pushbutton [package="[THT]"]
  R1 = Resistor [tolerance=±5% resistance=10k package=THT]

nets:
  N1: Componente1.5V, S1.Pin_1, S1.Pin_2
  N2: Componente1.GND, R1.Pin_0
  N3: Componente1.D2, S1.Pin_3, S1.Pin_4, R1.Pin_1
