# Fritzing sketch vect2dCircularDisplay (saved by Fritzing 0.8.3b)
breadboards: 1

parts:
  Componente1 = Arduino Uno (Rev3)
  R1 = Rotary Potentiometer (Small)
  R2 = Rotary Potentiometer (Small)
  LED1 = Adafruit_FLORA_RGB_Smart_Pixel

nets:
  N1: Componente1.A0, R1.wiper
  N2: Componente1.A1, R2.wiper
  N3: Componente1.GND, R1.leg2, R2.leg2, LED1.connector3
  N4: Componente1.D2, LED1.connector2
  N5: Componente1.5V, R1.leg1, R2.leg1, LED1.connector1
